# Fritzing sketch Water_level (saved by Fritzing 0.9.10b)

parts:
  IC1 = ULN2003A [package="DIP16 [THT]"]
  LED1 = smd LED [color="Red (633nm)" package="1206 [SMD]"]  # not connected
  LED3 = smd LED [color="Red (633nm)" package="1206 [SMD]"]  # not connected
  LED4 = smd LED [color="Green (555nm)" package="1206 [SMD]"]  # not connected
  LED5 = smd LED [color="Yellow (574nm)" package="1206 [SMD]"]  # not connected
  LED6 = smd LED [color="Green (555nm)" package="1206 [SMD]"]  # not connected
  LED7 = smd LED [color="White (4500K)" package="1206 [SMD]"]  # not connected
  R2 = Resistor [tolerance=±5% power=0.25 resistance=1k package=THT]  # not connected
  R3 = Resistor [tolerance=±5% power=0.25 resistance=1k package=THT]  # not connected
  R4 = Resistor [tolerance=±5% power=0.25 resistance=1k package=THT]  # not connected
  R5 = Resistor [tolerance=±5% power=0.25 resistance=1k package=THT]  # not connected
  R6 = Resistor [tolerance=±5% power=0.25 resistance=1k package=THT]  # not connected
  R7 = Resistor [tolerance=±5% power=0.25 resistance=1k package=THT]  # not connected
  R8 = Resistor [tolerance=±5% power=0.25 resistance=1k package=THT]  # not connected
  LED8 = smd LED [color="Yellow (574nm)" package="1206 [SMD]"]  # not connected
  VCC1 = Battery block 9V

nets:
  N1: IC1.0V, VCC1.-
